// Logisim project Logisim-CPU.circ as structural Verilog
module main (
);
endmodule

module J_K_FlipFlop__logisim (
  input  J,
  input  CLK,
  input  K,
  input  S,
  input  Enable,
  input  R,
  output Q
);

  J_K_Flip_Flop j_k_ff_1 (.J(J), .clk(CLK), .K(K), .Q(Q), .preset(S), .en(Enable), .reset(R));  // open: Qn

  // Notes on the sheet:
  //   J-K Flip Flop
endmodule

module Register_16Bit (
  input  S,
  input  Enable,
  input  CLK,
  input  R,
  input  E1,
  input  E2,
  input  E3,
  input  E4,
  input  E5,
  input  E6,
  input  E7,
  input  E8,
  output A1,
  output A2,
  output A3,
  output A4,
  output A5,
  output A6,
  output A7,
  output A8
);

  wire not_1_out, not_2_out, not_3_out, not_4_out, not_5_out, not_6_out, not_7_out, not_8_out;

  J_K_FlipFlop__logisim J_K_FlipFlop (.J(E1), .CLK(CLK), .K(not_1_out), .S(S), .Enable(Enable), .R(R), .Q(A1));
  not not_1 (not_1_out, E1);
  not not_2 (not_2_out, E5);
  J_K_FlipFlop__logisim J_K_FlipFlop_2 (.J(E5), .CLK(CLK), .K(not_2_out), .S(S), .Enable(Enable), .R(R), .Q(A5));
  not not_3 (not_3_out, E2);
  not not_4 (not_4_out, E6);
  J_K_FlipFlop__logisim J_K_FlipFlop_3 (.J(E2), .CLK(CLK), .K(not_3_out), .S(S), .Enable(Enable), .R(R), .Q(A2));
  J_K_FlipFlop__logisim J_K_FlipFlop_4 (.J(E6), .CLK(CLK), .K(not_4_out), .S(S), .Enable(Enable), .R(R), .Q(A6));
  not not_5 (not_5_out, E3);
  not not_6 (not_6_out, E7);
  J_K_FlipFlop__logisim J_K_FlipFlop_5 (.J(E3), .CLK(CLK), .K(not_5_out), .S(S), .Enable(Enable), .R(R), .Q(A3));
  J_K_FlipFlop__logisim J_K_FlipFlop_6 (.J(E7), .CLK(CLK), .K(not_6_out), .S(S), .Enable(Enable), .R(R), .Q(A7));
  not not_7 (not_7_out, E4);
  not not_8 (not_8_out, E8);
  J_K_FlipFlop__logisim J_K_FlipFlop_7 (.J(E4), .CLK(CLK), .K(not_7_out), .S(S), .Enable(Enable), .R(R), .Q(A4));
  J_K_FlipFlop__logisim J_K_FlipFlop_8 (.J(E8), .CLK(CLK), .K(not_8_out), .S(S), .Enable(Enable), .R(R), .Q(A8));
endmodule

module Register_16Bit__logisim (
  input  E1,
  input  E2,
  input  Enable,
  input  E3,
  input  E4,
  input  CLK,
  input  E5,
  input  E6,
  input  R,
  input  E7,
  input  E8,
  output A1,
  output A2,
  output A3,
  output A4,
  output A5,
  output A6,
  output A7,
  output A8
);

  Register register_1 (
    .D({E8, E7, E6, E5, E4, E3, E2, E1}), .en(Enable), .Q({A8, A7, A6, A5, A4, A3, A2, A1}), .clk(CLK),
    .clr(R));
endmodule

module J_K_FlipFlop (
  input  S,
  input  J,
  input  CLK,
  input  Enable,
  input  K,
  input  R,
  input  in_7,
  input  in_8,
  input  in_9,
  output A,
  output out_11
);

  wire AND_2_out, AND_3_out, AND_out, NAND_2_out, NAND_3_out, NAND_4_out, NAND_5_out, NAND_6_out, NAND_8_out,
       NAND_out, NOT_2_out, NOT_3_out, NOT_4_out, NOT_out;

  and AND (AND_out, CLK, Enable);
  not NOT (NOT_out, AND_out);
  and AND_2 (AND_2_out, in_7, in_8);
  not NOT_2 (NOT_2_out, S);
  nand NAND (NAND_out, NAND_8_out, J, NOT_out);
  nand NAND_2 (NAND_2_out, NOT_out, K, A);
  not NOT_3 (NOT_3_out, NOT_out);
  not NOT_4 (NOT_4_out, R);
  and AND_3 (AND_3_out, AND_2_out, in_9);
  not NOT_5 (out_11, AND_3_out);
  nand NAND_3 (NAND_3_out, NOT_2_out, NAND_out, NAND_4_out);
  nand NAND_4 (NAND_4_out, NAND_3_out, NAND_2_out, NOT_4_out);
  nand NAND_5 (NAND_5_out, NAND_3_out, NOT_3_out);
  nand NAND_6 (NAND_6_out, NOT_3_out, NAND_4_out);
  nand NAND_7 (A, NOT_2_out, NAND_5_out, NAND_8_out);
  nand NAND_8 (NAND_8_out, A, NAND_6_out, NOT_4_out);

  // Notes on the sheet:
  //   NAND (3 Eingänge)
endmodule

module HalbAddierer (
  input  E1,
  input  E2,
  output A,
  output U
);

  wire AND_2_out, AND_out, NOT_2_out, NOT_out;

  not NOT (NOT_out, E1);
  not NOT_2 (NOT_2_out, E2);
  and AND (AND_out, NOT_out, E2);
  and AND_2 (AND_2_out, NOT_2_out, E1);
  or OR (A, AND_out, AND_2_out);
  and AND_3 (U, E2, E1);
endmodule

module Volladdierer (
  input  E1,
  input  E2,
  input  Ue,
  output A,
  output Ua
);

  wire Halbaddierer_2_u, Halbaddierer_a, Halbaddierer_u;

  HalbAddierer Halbaddierer (.E1(E1), .E2(E2), .A(Halbaddierer_a), .U(Halbaddierer_u));
  HalbAddierer Halbaddierer_2 (.E1(Halbaddierer_a), .E2(Ue), .A(A), .U(Halbaddierer_2_u));
  or OR (Ua, Halbaddierer_2_u, Halbaddierer_u);
endmodule

module Addierer16Bit (
  input  Ue,
  input  X1,
  input  Y1,
  input  X2,
  input  Y2,
  input  X3,
  input  Y3,
  input  X4,
  input  Y4,
  input  X5,
  input  Y5,
  input  X6,
  input  Y6,
  input  X7,
  input  Y7,
  input  X8,
  input  Y8,
  output A1,
  output A2,
  output A3,
  output A4,
  output Ua,
  output A5,
  output A6,
  output A7,
  output A8
);

  wire Volladdierer_2_ua, Volladdierer_3_ua, Volladdierer_4_ua, Volladdierer_5_ua, Volladdierer_6_ua,
       Volladdierer_7_ua, Volladdierer_ua;

  Volladdierer Volladdierer (.E1(Y1), .E2(X1), .Ue(Ue), .A(A1), .Ua(Volladdierer_ua));
  Volladdierer Volladdierer_2 (.E1(Y5), .E2(X5), .Ue(Volladdierer_7_ua), .A(A5), .Ua(Volladdierer_2_ua));
  Volladdierer Volladdierer_3 (.E1(Y2), .E2(X2), .Ue(Volladdierer_ua), .A(A2), .Ua(Volladdierer_3_ua));
  Volladdierer Volladdierer_4 (.E1(Y6), .E2(X6), .Ue(Volladdierer_2_ua), .A(A6), .Ua(Volladdierer_4_ua));
  Volladdierer Volladdierer_5 (.E1(Y3), .E2(X3), .Ue(Volladdierer_3_ua), .A(A3), .Ua(Volladdierer_5_ua));
  Volladdierer Volladdierer_6 (.E1(Y7), .E2(X7), .Ue(Volladdierer_4_ua), .A(A7), .Ua(Volladdierer_6_ua));
  Volladdierer Volladdierer_7 (.E1(Y4), .E2(X4), .Ue(Volladdierer_5_ua), .A(A4), .Ua(Volladdierer_7_ua));
  Volladdierer Volladdierer_8 (.E1(Y8), .E2(X8), .Ue(Volladdierer_6_ua), .A(A8), .Ua(Ua));
endmodule

module Addierer16Bit_logisim (
  input  Ue,
  input  [7:0] X_1_8,
  input  [7:0] Y_1_8,
  output [7:0] A_1_8,
  output Ua
);

  Adder adder_1 (.a(X_1_8), .b(Y_1_8), .out(A_1_8), .cin(Ue), .cout(Ua));
endmodule

module ProgramCounter (
  input  PC_select,
  input  PC_load,
  input  Reset,
  input  [7:0] PC_in,
  output [7:0] PC_out
);

  wire Takt_out;
  wire [7:0] adder_1_out, multiplexer_1_out;

  Adder adder_1 (.a(PC_out), .b(8'h1), .out(adder_1_out), .cin(1'b0));  // open: cout
  Multiplexer #(.width(8), .enable("false")) multiplexer_1 (
    .in0(adder_1_out), .in1(PC_in), .out(multiplexer_1_out), .sel(PC_select));
  Clock Takt (.out(Takt_out));
  Register register_1 (.D(multiplexer_1_out), .en(PC_load), .Q(PC_out), .clk(Takt_out), .clr(Reset));

  // Notes on the sheet:
  //   Addierer
  //   Multiplexer
  //   Register
endmodule

module ALU_8Bit (
  input  [7:0] X,
  input  [7:0] Y,
  input  [1:0] OP_Select,
  output [7:0] A
);

  wire [7:0] adder_1_out, AND_8Bit_out, multiplexer_1_out, multiplexer_2_out, OR_8Bit_out, subtractor_1_out;

  assign AND_8Bit_out = X & Y;  // AND_Gate AND_8Bit, 8 bits wide
  assign OR_8Bit_out = X | Y;  // OR_Gate OR_8Bit, 8 bits wide
  Adder adder_1 (.a(X), .b(Y), .out(adder_1_out), .cin(1'b0));  // open: cout
  Subtractor subtractor_1 (.a(X), .b(Y), .out(subtractor_1_out), .bin(1'b0));  // open: bout
  Multiplexer #(.width(8), .enable("false")) multiplexer_1 (
    .in0(AND_8Bit_out), .in1(OR_8Bit_out), .out(multiplexer_1_out), .sel(OP_Select[1]));
  Multiplexer #(.width(8), .enable("false")) multiplexer_2 (
    .in0(adder_1_out), .in1(subtractor_1_out), .out(multiplexer_2_out), .sel(OP_Select[1]));
  Multiplexer #(.width(8), .enable("false")) multiplexer_3 (
    .in0(multiplexer_1_out), .in1(multiplexer_2_out), .out(A), .sel(OP_Select[0]));

  // Notes on the sheet:
  //   ADD 8Bit
  //   SUB 8Bit
endmodule

module AND_8Bit (
  input  [7:0] X,
  input  [7:0] Y,
  output [7:0] A
);

  and AND (A[0], X[0], Y[0]);
  and AND_2 (A[1], X[1], Y[1]);
  and AND_3 (A[2], X[2], Y[2]);
  and AND_4 (A[3], X[3], Y[3]);
  and AND_5 (A[4], X[4], Y[4]);
  and AND_6 (A[5], X[5], Y[5]);
  and AND_7 (A[6], X[6], Y[6]);
  and AND_8 (A[7], X[7], Y[7]);
endmodule

module OR_8Bit (
  input  [7:0] X,
  input  [7:0] B,
  output [7:0] A
);

  or OR (A[0], X[0], B[0]);
  or OR_2 (A[1], X[1], B[1]);
  or OR_3 (A[2], X[2], B[2]);
  or OR_4 (A[3], X[3], B[3]);
  or OR_5 (A[4], X[4], B[4]);
  or OR_6 (A[5], X[5], B[5]);
  or OR_7 (A[6], X[6], B[6]);
  or OR_8 (A[7], X[7], B[7]);
endmodule

module NOT_8Bit (
  input  [7:0] X,
  output [7:0] A
);

  not NOT (A[0], X[0]);
  not NOT_2 (A[1], X[1]);
  not NOT_3 (A[2], X[2]);
  not NOT_4 (A[3], X[3]);
  not NOT_5 (A[4], X[4]);
  not NOT_6 (A[5], X[5]);
  not NOT_7 (A[6], X[6]);
  not NOT_8 (A[7], X[7]);
endmodule

module Subtraktion_8Bit (
  input  [7:0] X,
  input  [7:0] Y,
  output [7:0] A
);

  wire [7:0] NOT_8Bit_out;

  assign NOT_8Bit_out = ~Y;  // NOT_Gate NOT_8Bit, 8 bits wide
  Adder adder_1 (.a(X), .b(NOT_8Bit_out), .out(A), .cin(1'b1));  // open: cout

  // Notes on the sheet:
  //   Ue
  //   Addierer
endmodule

module RegisterR1R2R3R4 (
  input  Write,
  input  [1:0] DestinationRegSelect,
  input  [7:0] DataIn,
  input  Takt,
  input  [1:0] SourceRegisterSelect,
  output [7:0] DestiantionBusOut,
  output ZeroFlag,
  output NegativFlag,
  output [7:0] SourceBusOut,
  output [7:0] R1,
  output [7:0] R2,
  output [7:0] R3,
  output [7:0] R4
);

  wire demultiplexer_1_out0, demultiplexer_1_out1, demultiplexer_1_out2, demultiplexer_1_out3, OR_8x_out;

  Demultiplexer #(.select(2), .enable("false")) demultiplexer_1 (
    .out0(demultiplexer_1_out0), .out1(demultiplexer_1_out1), .out2(demultiplexer_1_out2),
    .out3(demultiplexer_1_out3), .in(Write), .sel(DestinationRegSelect));
  Register register_1 (.D(DataIn), .en(demultiplexer_1_out0), .Q(R1), .clk(Takt));  // open: clr
  Register register_2 (.D(DataIn), .en(demultiplexer_1_out1), .Q(R2), .clk(Takt));  // open: clr
  Register register_3 (.D(DataIn), .en(demultiplexer_1_out2), .Q(R3), .clk(Takt));  // open: clr
  Register register_4 (.D(DataIn), .en(demultiplexer_1_out3), .Q(R4), .clk(Takt));  // open: clr
  Multiplexer #(.select(2), .width(8), .enable("false")) multiplexer_1 (
    .in0(R1), .in1(R2), .in2(R3), .in3(R4), .out(DestiantionBusOut), .sel(DestinationRegSelect));
  Multiplexer #(.select(2), .width(8), .enable("false")) multiplexer_2 (
    .in0(R1), .in1(R2), .in2(R3), .in3(R4), .out(SourceBusOut), .sel(SourceRegisterSelect));
  not NOT (ZeroFlag, OR_8x_out);
  or OR_8x (OR_8x_out, DestiantionBusOut[0], DestiantionBusOut[1], DestiantionBusOut[2], DestiantionBusOut[3], DestiantionBusOut[4], DestiantionBusOut[5], DestiantionBusOut[6], DestiantionBusOut[7]);

  assign NegativFlag = DestiantionBusOut[7];

  // Notes on the sheet:
  //   Demultiplexer
  //   R1
  //   R2
  //   R3
  //   R4
endmodule

module ALU_Reg (
  input  [7:0] Immediat,
  input  [7:0] DataIn,
  input  [1:0] RegSel,
  input  [1:0] dRegSel,
  input  [1:0] sRegSel,
  input  RegWrite,
  input  Takt,
  input  [1:0] OP_Select,
  output [7:0] sBus,
  output [7:0] DataIn_2,
  output ZeroFlag,
  output NegativFlag,
  output [7:0] dBus,
  output [7:0] AluOut,
  output [7:0] R1,
  output [7:0] R2,
  output [7:0] R3,
  output [7:0] R4
);

  Multiplexer #(.select(2), .width(8), .enable("false")) multiplexer_1 (
    .in0(Immediat), .in1(sBus), .in2(DataIn), .in3(AluOut), .out(DataIn_2), .sel(RegSel));
  RegisterR1R2R3R4 Register (
    .Write(RegWrite), .DestinationRegSelect(dRegSel), .DataIn(DataIn_2), .SourceRegisterSelect(sRegSel),
    .R1(R1), .Takt(Takt), .R2(R2), .R3(R3), .R4(R4), .DestiantionBusOut(dBus), .ZeroFlag(ZeroFlag),
    .NegativFlag(NegativFlag), .SourceBusOut(sBus));
  ALU_8Bit ALU (.X(dBus), .Y(sBus), .OP_Select(OP_Select), .A(AluOut));
endmodule

module Multiplexer_1Bit (
  input  E1,
  input  E2,
  input  S,
  output A
);

  wire AND_2_out, AND_out, NOT_out;

  not NOT (NOT_out, S);
  and AND (AND_out, E1, NOT_out);
  and AND_2 (AND_2_out, E2, S);
  or OR (A, AND_out, AND_2_out);
endmodule

module Multiplexer_8Bit (
  input  [7:0] E1,
  input  [7:0] E2,
  input  S,
  output [7:0] out_4
);

  Multiplexer_1Bit MUX_1Bit (.E1(E1[0]), .E2(E2[0]), .S(S), .A(out_4[0]));
  Multiplexer_1Bit MUX_1Bit_2 (.E1(E1[1]), .E2(E2[1]), .S(S), .A(out_4[1]));
  Multiplexer_1Bit MUX_1Bit_3 (.E1(E1[2]), .E2(E2[2]), .S(S), .A(out_4[2]));
  Multiplexer_1Bit MUX_1Bit_4 (.E1(E1[3]), .E2(E2[3]), .S(S), .A(out_4[3]));
  Multiplexer_1Bit MUX_1Bit_5 (.E1(E1[4]), .E2(E2[4]), .S(S), .A(out_4[4]));
  Multiplexer_1Bit MUX_1Bit_6 (.E1(E1[5]), .E2(E2[5]), .S(S), .A(out_4[5]));
  Multiplexer_1Bit MUX_1Bit_7 (.E1(E1[6]), .E2(E2[6]), .S(S), .A(out_4[6]));
  Multiplexer_1Bit MUX_1Bit_8 (.E1(E1[7]), .E2(S), .S(E2[7]), .A(out_4[7]));
endmodule

module DeMultiplexer_1Bit (
  input  E,
  input  S,
  output A1,
  output A2
);

  wire NOT_out;

  not NOT (NOT_out, S);
  and AND (A1, NOT_out, E);
  and AND_2 (A2, E, S);
endmodule

module DeMultiplexer_8Bit (
  input  [7:0] E,
  input  S,
  output [7:0] A1,
  output [7:0] A2
);

  DeMultiplexer_1Bit DeMUX_1Bit (.E(E[0]), .S(S), .A1(A1[0]), .A2(A2[0]));
  DeMultiplexer_1Bit DeMUX_1Bit_2 (.E(E[1]), .S(S), .A1(A1[1]), .A2(A2[1]));
  DeMultiplexer_1Bit DeMUX_1Bit_3 (.E(E[2]), .S(S), .A1(A1[2]), .A2(A2[2]));
  DeMultiplexer_1Bit DeMUX_1Bit_4 (.E(E[3]), .S(S), .A1(A1[3]), .A2(A2[3]));
  DeMultiplexer_1Bit DeMUX_1Bit_5 (.E(E[4]), .S(S), .A1(A1[4]), .A2(A2[4]));
  DeMultiplexer_1Bit DeMUX_1Bit_6 (.E(E[5]), .S(S), .A1(A1[5]), .A2(A2[5]));
  DeMultiplexer_1Bit DeMUX_1Bit_7 (.E(E[6]), .S(S), .A1(A1[6]), .A2(A2[6]));
  DeMultiplexer_1Bit DeMUX_1Bit_8 (.E(E[7]), .S(S), .A1(A1[7]), .A2(A2[7]));
endmodule
